# Fritzing sketch crane project (saved by Fritzing 0.9.3b)
circuit board: 8.46667cm x 5.64444cm

parts:
  Part1 = Arduino Nano (Rev3.0)
  U1 = LM2596 step down module
  S1 = Square Pushbutton
  U2 = 4-Channel 5v Relay Shield [package=relay-4ch5v10a]
  U3 = 2-Channel 5v Relay Shield [package=relay-2ch5v10a]
  JACK1 = 2.1mm DC Barrel Jack
  Mod1 = KY-023 Dual Axis Joystick Module [package="Breakout board"]
  Mod2 = KY-023 Dual Axis Joystick Module [package="Breakout board"]
  S4 = Limit Switch [package="Breakout Board"]
  S5 = Limit Switch [package="Breakout Board"]
  M1 = DC Motor
  M2 = DC Motor
  M3 = DC Motor
  J1 = female pin header, 2 pins [form="♀ (female)"]
  S6 = Square Pushbutton
  Part2 = LCD1602-I2C

nets:
  GND: Part1.GND, U1.IN-, U1.OUT-, U2.GND, U2.K1-In, JACK1.sleeve
  N1: Part1.D2, U3.IN1
  N2: Part1.D3, U3.IN2
  N3: Part1.D4, U2.IN1
  N4: Part1.D5, U2.IN2
  N5: Part1.D6, U2.IN3
  N6: Part1.D7, U2.IN4
  N7: Part1.D12/MISO, S5.S
  VIN: Part1.VIN, U1.OUT+, U2.VCC
  N8: Part1.A5, Part2.SCL
  N9: Part1.A4, Part2.SDA
  N10: Part1.A3, Mod1.VRy
  N11: Part1.A2, Mod1.VRx
  N12: Part1.A1, Mod2.VRy
  N13: Part1.A0, Mod2.VRx
  N14: Part1.D13/SCK, S4.S
  N15: U1.IN+, S1.leg1
  N16: S1.leg0, JACK1.center
  N17: U2.K1-Off, M3.pin_1
  N18: U2.K2-Off, M3.pin_2
  N19: U2.K3-Off, M2.pin_1
  N20: U2.K4-Off, M2.pin_2
  N21: U3.K1-In, M1.pin_1
  N22: U3.K2-In, M1.pin_2
  GND_2: Mod1.GND, Mod2.GND
  +5V: Mod1.+5V, Mod2.+5V
  N23: J1.pin2, S6.leg0

notes:
  dc jack
  limit switch 1
  6 channel relay
  buck converter
  on off button
  limit switch 2
  joy stickhw 504.
  #2
  joy stickhw 504.
  #1
  LCD 16*2
  nano
  dc motor 3
  dc motor 2
  dc motor 1
  electromagnetic module
  +
  -

custom parts:
  LM2596 step down module: LM2596 DC-DC step down power supply module 3 A.
  4-Channel 5v Relay Shield: 4 Channel 5v Relay Shield w. 2x SPD-06VDC-SD-C
  2-Channel 5v Relay Shield: 2 Channel 5v Relay Shield w. 2x SPD-06VDC-SD-C
  2.1mm DC Barrel Jack: 2.1mm DC Barrel Jack with Thru-Hole Connectors (breadboardable)
  KY-023 Dual Axis Joystick Module: KY-023 Dual-Axis Joystick Module.
  Limit Switch: Generic limit switch commonly found on 3D printers. Typical lever microswitch mounted on a PCB board with a 3 pin JST XH connector.
  LCD1602-I2C: A standard character display, usually with 2x16 characters. Comes in many colors with LCM1602 IIC attached.
